# Fritzing sketch Drone Electronics layout (saved by Fritzing 0.9.3b)

parts:
  U2 = mystery part, 12 pins [chip_label=?]  # not connected
  U1 = mystery part, 6 pins [chip_label=esc]  # not connected
  U4 = mystery part, 3 pins [chip_label=Motor]
  U5 = mystery part, 3 pins [chip_label=Motor]
  U6 = mystery part, 3 pins [chip_label=Motor]
  U7 = mystery part, 6 pins [chip_label=esc]
  U8 = mystery part, 6 pins [chip_label=esc]
  U9 = mystery part, 6 pins [chip_label=esc]
  U10 = mystery part, 6 pins [chip_label=esc]
  U11 = mystery part, 16 pins [chip_label=PDB]
  U11_2 = mystery part, 16 pins [chip_label=PDB]
  U11_3 = mystery part, 16 pins [chip_label=PDB]
  U12 = mystery part, 8 pins [chip_label="flight controller"]
  ANT1 = Antenna
  ANT2 = Antenna
  U13 = mystery part, 6 pins [chip_label=RX]
  U3 = mystery part, 3 pins [chip_label=Motor]
  U14 = LIPO-2000mAh [package=lipo-2000]
  Raspberry_Pi1 = Raspberry Pi B+  # not connected
  ANT3 = Antenna
  ANT4 = Antenna
  U16 = mystery part, 4 pins [chip_label=?]
  U15 = mystery part, 4 pins [chip_label="wifi dongle"]

nets:
  N1: U4.pin1, U7.pin3
  N2: U4.pin2, U7.pin2
  N3: U4.pin3, U7.pin1
  N4: U5.pin1, U8.pin3
  N5: U5.pin2, U8.pin2
  N6: U5.pin3, U8.pin1
  N7: U6.pin1, U9.pin6
  N8: U6.pin2, U9.pin5
  N9: U6.pin3, U9.pin4
  N10: U7.pin4, U11.pin8, U11_2.pin8, U11_3.pin8
  N11: U7.pin5, U12.pin4
  N12: U7.pin6, U11.pin7, U11_2.pin7, U11_3.pin7
  N13: U8.pin4, U11.pin2, U11_2.pin2, U11_3.pin2
  N14: U8.pin5, U12.pin1
  N15: U8.pin6, U11.pin1, U11_2.pin1, U11_3.pin1
  N16: U9.pin1, U11.pin10, U11_2.pin10, U11_3.pin10
  N17: U9.pin2, U12.pin5
  N18: U9.pin3, U11.pin9, U11_2.pin9, U11_3.pin9
  N19: U10.pin1, U11.pin16, U11_2.pin16, U11_3.pin16
  N20: U10.pin2, U12.pin8
  N21: U10.pin3, U11.pin15, U11_2.pin15, U11_3.pin15
  N22: U10.pin4, U3.pin3
  N23: U10.pin5, U3.pin2
  N24: U10.pin6, U3.pin1
  N25: U11_3.pin12, U14.+
  N26: U11_3.pin13, U14.-
  N27: U12.pin3, U13.pin3
  N28: U12.pin6, U13.pin2
  N29: U12.pin7, U13.pin1
  N30: ANT1.antenna_lead, U13.pin6
  N31: ANT2.antenna_lead, U13.pin4
  N32: ANT3.antenna_lead, U15.pin4
  N33: ANT4.antenna_lead, U16.pin3
